// Logisim project full adder and half adder using nand.circ as structural Verilog: 1 circuit, main circuit main
module main (
  input  in_1,
  input  in_2,
  input  in_3,
  input  in_4,
  input  in_5,
  input  in_6
);

  wire nand_1_out, nand_2_out, nand_3_out, nand_4_out, nand_5_out, nand_6_out, nand_7_out, nand_8_out,
       nand_9_out, nand_10_out, nand_11_out, nand_12_out, nand_13_out, nand_14_out, undriven;

  nand nand_1 (nand_1_out, in_1, in_2);
  nand nand_2 (nand_2_out, in_3, in_4);
  nand nand_3 (nand_3_out, nand_2_out, in_4);
  nand nand_4 (nand_4_out, in_1, nand_1_out);
  nand nand_5 (nand_5_out, nand_1_out, in_2);
  nand nand_6 (nand_6_out, in_3, nand_2_out);
  nand nand_7 (nand_7_out, nand_6_out, nand_3_out);
  LED led_1 (.in(nand_8_out));
  nand nand_8 (nand_8_out, nand_4_out, nand_5_out);
  nand nand_9 (nand_9_out, nand_1_out, nand_1_out);
  LED led_2 (.in(nand_9_out));
  nand nand_10 (nand_10_out, nand_7_out, in_5);
  nand nand_11 (nand_11_out, nand_7_out, nand_10_out);
  nand nand_12 (nand_12_out, nand_10_out, in_5);
  nand nand_13 (nand_13_out, nand_11_out, nand_12_out);
  nand nand_14 (nand_14_out, nand_10_out, nand_10_out, nand_2_out, undriven);
  LED led_3 (.in(nand_14_out));
  LED led_4 (.in(nand_13_out));
endmodule
