// Logisim project lab2.circ as structural Verilog: 1 circuit, main circuit main
module main (
  input  X,
  input  Y,
  input  in_3,
  input  in_4,
  input  C,
  input  A,
  input  B,
  input  A5,
  input  B5,
  input  in_10,
  input  Cin,
  input  A1,
  input  B1,
  input  A2,
  input  B2,
  input  A3,
  input  B3,
  input  A4,
  input  B4
);

  wire and_1_out, and_2_out, and_3_out, and_4_out, and_5_out, and_6_out, and_7_out, and_8_out, and_9_out,
       and_10_out, and_11_out, nand_1_out, nand_2_out, nand_3_out, nand_4_out, nand_5_out, nand_6_out,
       nand_7_out, nand_8_out, nand_9_out, nand_10_out, nand_11_out, nand_12_out, nand_13_out, nand_14_out,
       or_1_out, or_2_out, or_3_out, or_4_out, or_5_out, xor_1_out, xor_2_out, xor_3_out, xor_4_out,
       xor_5_out, xor_6_out, xor_7_out, xor_8_out, xor_9_out, xor_10_out, xor_11_out;

  xor xor_1 (xor_1_out, X, Y);
  LED led_1 (.in(xor_1_out));
  and and_1 (and_1_out, X, Y);
  LED led_2 (.in(and_1_out));
  xor xor_2 (xor_2_out, A, B);
  and and_2 (and_2_out, A, B);
  xor xor_3 (xor_3_out, A1, B1);
  and and_3 (and_3_out, A1, B1);
  xor xor_4 (xor_4_out, A2, B2);
  and and_4 (and_4_out, A2, B2);
  xor xor_5 (xor_5_out, A3, B3);
  and and_5 (and_5_out, A3, B3);
  xor xor_6 (xor_6_out, A4, B4);
  and and_6 (and_6_out, A4, B4);
  and and_7 (and_7_out, C, xor_2_out);
  xor xor_7 (xor_7_out, C, xor_2_out);
  LED sum (.in(xor_7_out));
  or or_1 (or_1_out, and_7_out, and_2_out);
  xor xor_8 (xor_8_out, Cin, xor_3_out);
  LED S1 (.in(xor_8_out));
  and and_8 (and_8_out, Cin, xor_3_out);
  xor xor_9 (xor_9_out, or_2_out, xor_4_out);
  LED S2 (.in(xor_9_out));
  and and_9 (and_9_out, or_2_out, xor_4_out);
  xor xor_10 (xor_10_out, or_3_out, xor_5_out);
  LED S3 (.in(xor_10_out));
  and and_10 (and_10_out, or_3_out, xor_5_out);
  xor xor_11 (xor_11_out, or_4_out, xor_6_out);
  LED S4 (.in(xor_11_out));
  and and_11 (and_11_out, or_4_out, xor_6_out);
  LED Cout (.in(or_1_out));
  or or_2 (or_2_out, and_8_out, and_3_out);
  nand nand_1 (nand_1_out, in_3, in_4);
  or or_3 (or_3_out, and_9_out, and_4_out);
  or or_4 (or_4_out, and_10_out, and_5_out);
  or or_5 (or_5_out, and_11_out, and_6_out);
  LED C_out (.in(or_5_out));
  nand nand_2 (nand_2_out, in_3, nand_1_out);
  nand nand_3 (nand_3_out, nand_1_out, in_4);
  nand nand_4 (nand_4_out, A5, B5);
  nand nand_5 (nand_5_out, nand_2_out, nand_3_out);
  nand nand_6 (nand_6_out, nand_1_out, nand_1_out);
  nand nand_7 (nand_7_out, A5, nand_4_out);
  nand nand_8 (nand_8_out, nand_4_out, B5);
  LED led_3 (.in(nand_5_out));
  LED led_4 (.in(nand_6_out));
  nand nand_9 (nand_9_out, nand_7_out, nand_8_out);
  nand nand_10 (nand_10_out, nand_9_out, in_10);
  nand nand_11 (nand_11_out, nand_9_out, nand_10_out);
  nand nand_12 (nand_12_out, nand_10_out, in_10);
  nand nand_13 (nand_13_out, nand_11_out, nand_12_out);
  nand nand_14 (nand_14_out, nand_10_out, nand_4_out);
  LED add (.in(nand_13_out));
  LED led_5 (.in(nand_14_out));

  // Notes on the sheet:
  //   Half Adder
  //   Full Adder
  //   4 Bit Adder
  //   Half Adder using NAND gate
  //   Full Adder using NAND gate
endmodule
