// Logisim project lab4.circ as structural Verilog: 1 circuit, main circuit main
module main (
  input  Cin,
  input  in_2,
  input  A1,
  input  in_4,
  input  in_5,
  input  in_6,
  input  in_7,
  input  in_8,
  input  in_9,
  input  A2,
  input  in_11,
  input  B2,
  input  A3,
  input  B3,
  input  A4,
  input  B4,
  output S1,
  output out_18,
  output out_19,
  output out_20,
  output out_21,
  output S2,
  output out_23,
  output S3,
  output S4,
  output Cout
);

  wire adder_1_cout, adder_2_cout, adder_3_cout, and_1_out, and_2_out, and_3_out, and_4_out, and_5_out,
       and_6_out, and_7_out, and_8_out, B1_out, clock_1_out, or_1_out, or_2_out, or_3_out, xor_1_out,
       xor_2_out, xor_3_out, xor_4_out;

  Clock B1 (.out(B1_out));
  and and_1 (and_1_out, A1, B1_out);
  xor xor_1 (xor_1_out, A1, B1_out);
  xor xor_2 (xor_2_out, A2, B2);
  and and_2 (and_2_out, A2, B2);
  xor xor_3 (xor_3_out, A3, B3);
  and and_3 (and_3_out, A3, B3);
  xor xor_4 (xor_4_out, A4, B4);
  and and_4 (and_4_out, A4, B4);
  xor xor_5 (S1, Cin, xor_1_out);
  and and_5 (and_5_out, Cin, xor_1_out);
  xor xor_6 (S2, or_1_out, xor_2_out);
  and and_6 (and_6_out, or_1_out, xor_2_out);
  xor xor_7 (S3, or_2_out, xor_3_out);
  and and_7 (and_7_out, or_2_out, xor_3_out);
  xor xor_8 (S4, or_3_out, xor_4_out);
  and and_8 (and_8_out, or_3_out, xor_4_out);
  or or_1 (or_1_out, and_5_out, and_1_out);
  or or_2 (or_2_out, and_6_out, and_2_out);
  or or_3 (or_3_out, and_7_out, and_3_out);
  or or_4 (Cout, and_8_out, and_4_out);
  Clock clock_1 (.out(clock_1_out));
  Adder #(.width(1)) adder_1 (.a(in_4), .b(clock_1_out), .out(out_18), .cin(in_2), .cout(adder_1_cout));
  Adder #(.width(1)) adder_2 (.a(in_5), .b(in_6), .out(out_19), .cin(adder_1_cout), .cout(adder_2_cout));
  Adder #(.width(1)) adder_3 (.a(in_7), .b(in_8), .out(out_20), .cin(adder_2_cout), .cout(adder_3_cout));
  Adder #(.width(1)) adder_4 (.a(in_9), .b(in_11), .out(out_21), .cin(adder_3_cout), .cout(out_23));
  // Digital_Oscilloscope digital_oscilloscope_1: pin names not known; wires that end beside it: out_18, out_23
endmodule
