// Logisim project lab_3.circ as structural Verilog: 1 circuit, main circuit main
module main (
  input  I7,
  input  I6,
  input  I5,
  input  I4,
  input  I3,
  input  I2,
  input  I1,
  input  I0,
  input  S2,
  input  S1,
  input  S0,
  input  in_12,
  input  in_13,
  input  in_14,
  input  in_15,
  input  in_16,
  input  in_17,
  input  in_18,
  input  [2:0] in_19,
  input  in_20,
  input  l7,
  input  l6,
  input  l5,
  input  l4,
  input  l3,
  input  l2,
  input  l1,
  input  l0,
  output out_29,
  output out_30,
  output A0,
  output A1,
  output A2
);

  wire and_1_out, and_2_out, and_3_out, and_4_out, and_5_out, and_6_out, and_7_out, and_8_out, and_9_out,
       and_10_out, and_11_out, and_12_out, and_13_out, and_14_out, and_15_out, and_16_out, and_17_out,
       and_18_out, and_19_out, and_20_out, and_21_out, and_22_out, and_23_out, and_24_out, not_1_out,
       not_2_out, not_3_out, or_1_out, or_2_out, or_3_out, or_4_out, or_5_out, or_6_out, or_10_out,
       or_11_out, or_12_out, or_13_out, or_14_out, or_15_out;

  not not_1 (not_1_out, S2);
  not not_2 (not_2_out, S1);
  or or_1 (or_1_out, l1, l3);
  or or_2 (or_2_out, l5, l7);
  or or_3 (or_3_out, l2, l3);
  or or_4 (or_4_out, l6, l7);
  or or_5 (or_5_out, l4, l5);
  or or_6 (or_6_out, l6, l7);
  not not_3 (not_3_out, S0);
  or or_7 (A0, or_1_out, or_2_out);
  or or_8 (A1, or_3_out, or_4_out);
  or or_9 (A2, or_5_out, or_6_out);
  and and_1 (and_1_out, not_3_out, not_2_out);
  and and_2 (and_2_out, not_1_out, I0);
  and and_3 (and_3_out, S0, not_2_out);
  and and_4 (and_4_out, not_1_out, I1);
  and and_5 (and_5_out, not_3_out, S1);
  and and_6 (and_6_out, not_1_out, I2);
  and and_7 (and_7_out, S0, S1);
  and and_8 (and_8_out, not_1_out, I3);
  and and_9 (and_9_out, not_3_out, not_2_out);
  and and_10 (and_10_out, S2, I4);
  and and_11 (and_11_out, S0, not_2_out);
  and and_12 (and_12_out, S2, I5);
  and and_13 (and_13_out, not_3_out, S1);
  and and_14 (and_14_out, S2, I6);
  and and_15 (and_15_out, S0, S1);
  and and_16 (and_16_out, S2, I7);
  and and_17 (and_17_out, and_1_out, and_2_out);
  and and_18 (and_18_out, and_3_out, and_4_out);
  and and_19 (and_19_out, and_5_out, and_6_out);
  and and_20 (and_20_out, and_7_out, and_8_out);
  and and_21 (and_21_out, and_9_out, and_10_out);
  and and_22 (and_22_out, and_11_out, and_12_out);
  and and_23 (and_23_out, and_13_out, and_14_out);
  and and_24 (and_24_out, and_15_out, and_16_out);
  or or_10 (or_10_out, and_17_out, and_18_out);
  or or_11 (or_11_out, and_19_out, and_20_out);
  or or_12 (or_12_out, and_21_out, and_22_out);
  or or_13 (or_13_out, and_23_out, and_24_out);
  or or_14 (or_14_out, or_10_out, or_11_out);
  or or_15 (or_15_out, or_12_out, or_13_out);
  or or_16 (out_29, or_14_out, or_15_out);
  Multiplexer #(.select(3)) multiplexer_1 (
    .in0(in_12), .in1(in_13), .in2(in_14), .in3(in_15), .in4(in_16), .in5(in_17), .in6(in_18), .in7(in_20),
    .out(out_30), .sel(in_19));

  // Notes on the sheet:
  //   8x3 Encoder
  //   8X1 MUX using basic gates
  //   8x3 MUX
endmodule
